// Logisim project PB1204microcode.circ as structural Verilog: 1 circuit, main circuit main
module main (
  input  [3:0] DATA,
  input  [3:0] RegisterNumber,
  input  [3:0] FunctionNumber,
  input  in_4,
  input  in_5
);

  wire and_1_out, and_2_out, and_3_out, and_4_out, and_5_out, and_6_out, and_7_out, and_8_out, and_9_out,
       and_10_out, and_11_out, and_12_out, and_13_out, and_14_out, and_15_out, and_16_out, and_17_out,
       and_18_out, and_19_out, ARegisterEnable, BitmaskRegisterEnable, BorrowFlag, BorrowFlagEnable,
       BRegisterEnable, BufferRegisterEnable, CarryFlag, CarryFlagEnable, CheckIfFlag, clock_1_out,
       DecrementRegister, IncrementRegister, InstructionRegisterEnable, InterruptModeRegisterEnable,
       not_2_out, OddParityFlag, OddParityFlagEnable, or_1_out, or_2_out, or_3_out, or_4_out, or_5_out,
       or_6_out, or_7_out, PC0_carry, PC0Enable, PC1_carry, PC1Enable, PC2Enable, ReadFromDatabus,
       ResetRegister, s_r_ff_1_q, SkipMicrocode, SP0Enable, SP1Enable, SP2Enable, TriggerUpdateOfRegister,
       WriteToAddressRegister, WriteToDatabus, xor_1_out, xor_2_out, xor_3_out, ZeroFlag, ZeroFlagEnable;
  wire [3:0] AData, ALUData, BData, BufferData, controlled_buffer_1_out, DATABUS, PC0Data, PC1Data, PC2Data,
       SP0Data, SP1Data, SP2Data;

  xor xor_1 (xor_1_out, AData[0], AData[1]);
  xor xor_2 (xor_2_out, AData[2], AData[3]);
  nor nor_1 (ZeroFlag, AData[0], AData[1], AData[2], AData[3]);
  xor xor_3 (xor_3_out, xor_1_out, xor_2_out);
  Register #(.width(4)) BufferRegister (
    .D(controlled_buffer_1_out), .en(BufferRegisterEnable), .clk(or_1_out), .Q(BufferData));  // open: clr
  assign controlled_buffer_1_out = TriggerUpdateOfRegister ? ALUData : 4'bz;  // Controlled_Buffer controlled_buffer_1
  or or_1 (or_1_out, TriggerUpdateOfRegister, ReadFromDatabus);
  assign controlled_buffer_1_out = ReadFromDatabus ? DATABUS : 4'bz;  // Controlled_Buffer controlled_buffer_2
  not not_1 (OddParityFlag, xor_3_out);
  D_Flip_Flop u_CarryFlag (.Q(CarryFlag));  // open: D, clk, Qn, preset, reset
  D_Flip_Flop u_BorrowFlag (.Q(BorrowFlag));  // open: D, clk, Qn, preset, reset
  and and_1 (and_1_out, WriteToDatabus, ARegisterEnable);
  and and_2 (and_2_out, WriteToDatabus, PC0Enable);
  and and_3 (and_3_out, WriteToDatabus, PC1Enable);
  assign DATABUS = and_1_out ? AData : 4'bz;  // Controlled_Buffer controlled_buffer_3
  assign DATABUS = and_2_out ? PC0Data : 4'bz;  // Controlled_Buffer controlled_buffer_4
  assign DATABUS = and_3_out ? PC1Data : 4'bz;  // Controlled_Buffer controlled_buffer_5
  and and_4 (and_4_out, WriteToDatabus, PC2Enable);
  and and_5 (and_5_out, WriteToDatabus, BRegisterEnable);
  and and_6 (and_6_out, WriteToDatabus, SP0Enable);
  assign DATABUS = and_4_out ? PC2Data : 4'bz;  // Controlled_Buffer controlled_buffer_6
  assign DATABUS = and_5_out ? BData : 4'bz;  // Controlled_Buffer controlled_buffer_7
  assign DATABUS = and_6_out ? SP0Data : 4'bz;  // Controlled_Buffer controlled_buffer_8
  Register #(.width(4)) ARegister (
    .D(BufferData), .en(ARegisterEnable), .clk(TriggerUpdateOfRegister), .Q(AData));  // open: clr
  Register #(.width(4)) BRegister (
    .D(BufferData), .en(BRegisterEnable), .clk(TriggerUpdateOfRegister), .Q(BData));  // open: clr
  and and_7 (and_7_out, WriteToDatabus, SP2Enable);
  and and_8 (and_8_out, WriteToDatabus, SP1Enable);
  assign DATABUS = and_8_out ? SP1Data : 4'bz;  // Controlled_Buffer controlled_buffer_9
  assign DATABUS = and_7_out ? SP2Data : 4'bz;  // Controlled_Buffer controlled_buffer_10
  Register #(.width(4)) InstructionRegister (
    .D(BufferData), .en(InstructionRegisterEnable), .clk(TriggerUpdateOfRegister));  // open: Q, clr
  Register #(.width(4)) BitmaskRegister (
    .D(BufferData), .en(BitmaskRegisterEnable), .clk(TriggerUpdateOfRegister));  // open: Q, clr
  Register #(.width(4)) InterruptModeRegister (
    .D(BufferData), .en(InterruptModeRegisterEnable), .clk(TriggerUpdateOfRegister));  // open: Q, clr
  Clock clock_1 (.out(clock_1_out));
  S_R_Flip_Flop HasBitmaskBeenSet ();  // open: S, R, clk, Q, reset, Qn, preset
  Demultiplexer #(.select(4)) demultiplexer_1 (
    .out0(InstructionRegisterEnable), .out1(BitmaskRegisterEnable), .out2(BufferRegisterEnable),
    .out3(InterruptModeRegisterEnable), .out4(ZeroFlagEnable), .out5(CarryFlagEnable),
    .out6(BorrowFlagEnable), .out7(OddParityFlagEnable), .out8(ARegisterEnable), .out9(PC0Enable),
    .out10(PC1Enable), .out11(PC2Enable), .out12(BRegisterEnable), .out13(SP0Enable), .out14(SP1Enable),
    .out15(SP2Enable), .in(in_5), .sel(RegisterNumber));
  and and_9 (and_9_out, SkipMicrocode, clock_1_out);
  Demultiplexer #(.select(4)) demultiplexer_2 (
    .out0(ReadFromDatabus), .out1(WriteToDatabus), .out2(WriteToAddressRegister),
    .out3(TriggerUpdateOfRegister), .out4(IncrementRegister), .out5(DecrementRegister), .out6(CheckIfFlag),
    .out7(ResetRegister), .in(and_9_out), .sel(FunctionNumber));  // open: out8, out9, out10, out11, out12, out13, out14, out15
  S_R_Flip_Flop s_r_ff_1 (
    .Q(s_r_ff_1_q), .reset(DecrementRegister), .preset(IncrementRegister));  // open: S, R, clk, Qn
  or or_2 (or_2_out, IncrementRegister, DecrementRegister);
  and and_10 (and_10_out, PC2Enable, TriggerUpdateOfRegister);
  and and_11 (and_11_out, PC1Enable, TriggerUpdateOfRegister);
  and and_12 (and_12_out, PC0Enable, TriggerUpdateOfRegister);
  and and_13 (and_13_out, PC0Enable, or_2_out);
  or or_3 (or_3_out, and_10_out, PC1_carry);
  or or_4 (or_4_out, and_11_out, PC0_carry);
  or or_5 (or_5_out, and_12_out, and_13_out, in_4);
  Counter #(.max('hf), .width(4)) PC2 (
    .load(and_10_out), .up(s_r_ff_1_q), .count(1'b1), .clk(or_3_out), .D(BufferData), .Q(PC2Data));  // open: clr, carry
  Counter #(.max('hf), .width(4)) PC1 (
    .load(and_11_out), .up(s_r_ff_1_q), .count(1'b1), .clk(or_4_out), .D(BufferData), .carry(PC1_carry),
    .Q(PC1Data));  // open: clr
  Counter #(.max('hf), .width(4)) PC0 (
    .load(and_12_out), .up(s_r_ff_1_q), .count(1'b1), .clk(or_5_out), .D(BufferData), .carry(PC0_carry),
    .Q(PC0Data));  // open: clr
  and and_14 (and_14_out, ZeroFlag, ZeroFlagEnable);
  and and_15 (and_15_out, CarryFlag, CarryFlagEnable);
  and and_16 (and_16_out, BorrowFlag, BorrowFlagEnable);
  and and_17 (and_17_out, OddParityFlag, OddParityFlagEnable);
  or or_6 (or_6_out, and_14_out, and_15_out, and_16_out, and_17_out);
  and and_18 (and_18_out, CheckIfFlag, or_6_out);
  not not_2 (not_2_out, FunctionNumber[3]);
  S_R_Flip_Flop s_r_ff_2 (.Q(SkipMicrocode), .reset(and_19_out), .preset(and_18_out));  // open: S, R, clk, Qn
  and and_19 (and_19_out, FunctionNumber[0], FunctionNumber[1], FunctionNumber[2], not_2_out);
  Register #(.width(12)) AddressRegister (.D({PC0Data, PC1Data, PC2Data}), .clk(or_7_out));  // open: en, Q, clr
  // OR_Gate or_7 has open pins: out=or_7_out

  // Other names for the same wires on the sheet: FuncID[3:0] = FunctionNumber; RegID[3:0] = RegisterNumber

  // Notes on the sheet:
  //   Passive Flags
  //   Active Flags
  //   Arithmetic Registers
  //   Register Outputs to Databus
  //   Decoder
  //   ALU
  //   If Reset Register Instruction is called
  //   Conditionals
  //   Skip remaining Microcode until Reset
endmodule
