// Logisim project PBP1204.circ as structural Verilog: 1 circuit, main circuit main
module main (
  input  ManualMode,
  input  [3:0] Action,
  input  [3:0] Location
);

  wire AAD, adder_1_cout, ANA, and_1_out, and_2_out, and_4_out, and_5_out, and_6_out, and_7_out, and_8_out,
       and_9_out, and_10_out, and_11_out, and_12_out, and_13_out, and_14_out, and_15_out, and_16_out,
       and_17_out, and_18_out, and_19_out, and_20_out, and_21_out, and_22_out, and_23_out, and_24_out,
       and_25_out, and_26_out, and_27_out, and_28_out, and_29_out, and_32_out, and_33_out, and_34_out,
       and_35_out, and_36_out, and_37_out, and_38_out, and_39_out, and_40_out, and_41_out, and_42_out,
       and_43_out, and_44_out, and_45_out, and_46_out, ANO, ANT, ARenable, ASL, ASR, BMenable, BMset,
       BorrowFlag, BorrowFlagReset, BRenable, CarryFlag, CarryFlagReset, CLK, clock_2_out, comparator_1_lt,
       comparator_2_eq, comparator_3_eq, CTF, CycleFinished, DEC, demultiplexer_2_out15,
       demultiplexer_3_out8, demultiplexer_3_out9, demultiplexer_3_out10, demultiplexer_3_out12,
       demultiplexer_3_out13, demultiplexer_3_out14, demultiplexer_4_out0, demultiplexer_4_out1,
       demultiplexer_4_out2, demultiplexer_4_out3, demultiplexer_4_out4, demultiplexer_4_out5,
       demultiplexer_4_out6, demultiplexer_4_out7, EvenParityFlag, FlagResult, HBenable, HPCenable,
       HSPenable, INC, INTenable, IRenable, LBenable, LPCenable, LSPenable, MBenable, MPCenable, MSPenable,
       nor_1_out, not_1_out, not_2_out, not_3_out, not_4_out, not_5_out, not_6_out, not_7_out, not_8_out,
       not_10_out, not_11_out, not_12_out, not_13_out, not_14_out, not_15_out, not_16_out, or_3_out,
       or_4_out, or_5_out, or_6_out, or_7_out, or_9_out, or_10_out, or_11_out, or_12_out, or_13_out,
       or_15_out, or_16_out, or_17_out, or_18_out, or_19_out, or_20_out, or_21_out, pull_resistor_1_node,
       pull_resistor_6_node, pull_resistor_8_node, pull_resistor_9_node, pull_resistor_10_node,
       pull_resistor_11_node, pull_resistor_12_node, pull_resistor_13_node, RBR, RDB, Read, RESET, RRD, RSF,
       ShortWideInst, TFenable, UAR, WBR, WDB, xor_1_out, xor_2_out, xor_3_out, ZeroFlag;
  wire [2:0] controlled_buffer_17_out, TestFlagsRegister_q;
  wire [3:0] ALUresult, AReg, BitmaskReg, BReg, DATA, HiBuffer_q, InstructionRegister_q, LowBuffer_q,
       MicrocodeLocation, MidBuffer_q, pull_resistor_5_node, rom_1_data;
  wire [4:0] InstructionCounter_q;
  wire [7:0] controlled_buffer_2_out, Microcode_data;
  wire [9:9] and_3_out;
  wire [11:0] ADDRESS, AddressBuffer, controlled_buffer_19_out, ProgramCounter, StackPointer;

  and and_1 (and_1_out, RRD, IRenable);
  or or_1 (Read, pull_resistor_1_node, RDB);
  or or_2 (CycleFinished, and_1_out, RESET);
  // LedBar #(.inputtype("row"), .matrixcols(12)) ledbar_1: pin names not known; wires that end beside it: ADDRESS
  // LedBar #(.inputtype("row"), .matrixcols(4)) ledbar_2: pin names not known; wires that end beside it: DATA
  Clock clock_1 (.out(CLK));
  Pull_Resistor pull_resistor_1 (.node(pull_resistor_1_node));
  POR por_1 (.out(RESET));
  // LedBar #(.inputtype("row"), .matrixcols(4)) ledbar_3: pin names not known; wires that end beside it: {Read, WDB, RESET, CLK}
  Counter #(.max('h1f), .trigger("falling"), .width(5)) InstructionCounter (
    .clr(CycleFinished), .load(1'b0), .up(1'b1), .count(1'b1), .clk(CLK), .Q(InstructionCounter_q));  // open: D, carry
  Register #(.trigger("falling"), .width(4)) InstructionRegister (
    .D(DATA), .en(IRenable), .clk(CLK), .Q(InstructionRegister_q), .clr(CycleFinished));
  Pull_Resistor pull_resistor_2 (.node(DATA));
  Pull_Resistor pull_resistor_3 (.node(ADDRESS));
  Comparator #(.mode("unsigned"), .width(4)) comparator_1 (
    .a(InstructionRegister_q), .b(4'b0101), .lt(comparator_1_lt));  // open: gt, eq
  and and_2 (and_2_out, CLK, ADDRESS[11]);
  ROM #(.addrWidth(10)) Microcode (
    .addr({and_3_out[9], InstructionRegister_q, InstructionCounter_q}), .data(Microcode_data));
  and and_3 (and_3_out[9], ShortWideInst, comparator_1_lt);
  RAM #(.addrWidth(11), .dataWidth(4), .databus("bidir"), .trigger("falling")) ram_1 (
    .addr(ADDRESS[10:0]), .we(WDB), .oe(Read), .clk(and_2_out), .data(DATA));
  ROM #(.addrWidth(11), .dataWidth(4)) rom_1 (.addr(ADDRESS[10:0]), .data(rom_1_data));
  Hex_Digit_Display #(.decimalPoint("false")) A (.value(AReg));
  // LedBar #(.inputtype("row"), .matrixcols(4)) ledbar_4: pin names not known
  // LedBar #(.inputtype("row"), .matrixcols(4)) ledbar_5: pin names not known
  // LedBar #(.inputtype("row"), .matrixcols(12)) ledbar_6: pin names not known; wires that end beside it: ProgramCounter
  // LedBar #(.inputtype("row"), .matrixcols(12)) ledbar_7: pin names not known; wires that end beside it: StackPointer
  // Probe on {and_3_out[9], InstructionRegister_q, InstructionCounter_q}
  Hex_Digit_Display #(.decimalPoint("false")) B (.value(BReg));
  not not_1 (not_1_out, ADDRESS[11]);
  Hex_Digit_Display #(.decimalPoint("false")) hex_digit_display_1 (.value(ADDRESS[11:8]));
  Hex_Digit_Display #(.decimalPoint("false")) hex_digit_display_2 (.value(ADDRESS[7:4]));
  and and_4 (and_4_out, not_1_out, Read);
  assign DATA = and_4_out ? rom_1_data : 4'bz;  // Controlled_Buffer controlled_buffer_1
  Hex_Digit_Display #(.decimalPoint("false")) hex_digit_display_3 (.value(ADDRESS[3:0]));
  assign controlled_buffer_2_out = ManualMode ? {Location, Action} : 8'bz;  // Controlled_Buffer controlled_buffer_2
  not not_2 (not_2_out, ManualMode);
  assign controlled_buffer_2_out = not_2_out ? Microcode_data : 8'bz;  // Controlled_Buffer controlled_buffer_3
  not not_3 (not_3_out, RSF);
  Demultiplexer #(.select(4)) demultiplexer_1 (
    .out0(RDB), .out1(WDB), .out2(RBR), .out3(WBR), .out4(RSF), .out5(UAR), .out6(CTF), .out7(RRD),
    .out8(ANA), .out9(ANO), .out10(ANT), .out11(AAD), .out12(ASL), .out13(ASR), .out14(INC), .out15(DEC),
    .in(CLK), .sel(controlled_buffer_2_out[3:0]));
  and and_5 (and_5_out, not_3_out, CLK);
  Demultiplexer #(.select(4)) demultiplexer_2 (
    .out0(IRenable), .out1(LBenable), .out2(MBenable), .out3(HBenable), .out4(ARenable), .out5(BRenable),
    .out6(TFenable), .out7(BMenable), .out8(LPCenable), .out9(MPCenable), .out10(HPCenable),
    .out11(INTenable), .out12(LSPenable), .out13(MSPenable), .out14(HSPenable),
    .out15(demultiplexer_2_out15), .in(and_5_out), .sel(MicrocodeLocation));
  Pull_Resistor pull_resistor_4 (.node(MicrocodeLocation));
  assign MicrocodeLocation = not_4_out ? controlled_buffer_2_out[7:4] : 4'bz;  // Controlled_Buffer controlled_buffer_4
  not not_4 (not_4_out, comparator_2_eq);
  Comparator #(.mode("unsigned"), .width(4)) comparator_2 (
    .a(controlled_buffer_2_out[7:4]), .b(4'b1111), .eq(comparator_2_eq));  // open: gt, lt
  assign MicrocodeLocation = comparator_2_eq ? BitmaskReg : 4'bz;  // Controlled_Buffer controlled_buffer_5
  not not_5 (not_5_out, WDB);
  and and_6 (and_6_out, not_5_out, LBenable);
  and and_7 (and_7_out, CLK, BMenable);
  Pull_Resistor pull_resistor_5 (.node(pull_resistor_5_node));
  assign pull_resistor_5_node = AAD ? ALUresult : 4'bz;  // Controlled_Buffer controlled_buffer_6
  assign pull_resistor_5_node = RDB ? DATA : 4'bz;  // Controlled_Buffer controlled_buffer_7
  and and_8 (and_8_out, ARenable, WBR);
  assign pull_resistor_5_node = and_8_out ? AReg : 4'bz;  // Controlled_Buffer controlled_buffer_8
  and and_9 (and_9_out, BRenable, WBR);
  assign pull_resistor_5_node = and_9_out ? BReg : 4'bz;  // Controlled_Buffer controlled_buffer_9
  or or_3 (or_3_out, and_9_out, and_6_out, and_8_out);
  or or_4 (or_4_out, RESET, CycleFinished);
  Counter #(.max('hf), .trigger("falling"), .width(4)) BitmaskRegister (
    .clr(or_4_out), .load(not_6_out), .up(pull_resistor_6_node), .count(INC), .clk(and_7_out), .D(DATA),
    .Q(BitmaskReg));  // open: carry
  not not_6 (not_6_out, INC);
  Pull_Resistor #(.pull(1)) pull_resistor_6 (.node(pull_resistor_6_node));
  and and_10 (and_10_out, LBenable, UAR);
  Register #(.trigger("falling"), .width(4)) LowBuffer (
    .D(pull_resistor_5_node), .en(or_3_out), .clk(CLK), .Q(LowBuffer_q), .clr(RESET));
  Register #(.trigger("falling"), .width(4)) MidBuffer (
    .D(pull_resistor_5_node), .en(MBenable), .clk(CLK), .Q(MidBuffer_q), .clr(RESET));
  Register #(.trigger("falling"), .width(4)) HiBuffer (
    .D(pull_resistor_5_node), .en(HBenable), .clk(CLK), .Q(HiBuffer_q), .clr(RESET));
  not not_7 (not_7_out, WBR);
  assign AddressBuffer[3:0] = INC ? BReg : 4'bz;  // Controlled_Buffer controlled_buffer_10
  or or_5 (or_5_out, and_10_out, FlagResult, RBR);
  and and_11 (and_11_out, not_7_out, TFenable);
  and and_12 (and_12_out, TFenable, RRD);
  assign AddressBuffer[3:0] = or_5_out ? LowBuffer_q : 4'bz;  // Controlled_Buffer controlled_buffer_11
  assign AddressBuffer[7:4] = or_5_out ? MidBuffer_q : 4'bz;  // Controlled_Buffer controlled_buffer_12
  assign AddressBuffer[11:8] = or_5_out ? HiBuffer_q : 4'bz;  // Controlled_Buffer controlled_buffer_13
  and and_13 (and_13_out, CTF, CLK);
  and and_14 (and_14_out, CLK, RSF);
  Register #(.trigger("falling"), .width(3)) TestFlagsRegister (
    .D(pull_resistor_5_node[2:0]), .en(and_11_out), .clk(CLK), .Q(TestFlagsRegister_q), .clr(or_6_out));
  or or_6 (or_6_out, and_12_out, RESET);
  assign DATA = and_17_out ? LowBuffer_q : 4'bz;  // Controlled_Buffer controlled_buffer_14
  assign DATA = and_16_out ? MidBuffer_q : 4'bz;  // Controlled_Buffer controlled_buffer_15
  assign DATA = and_15_out ? HiBuffer_q : 4'bz;  // Controlled_Buffer controlled_buffer_16
  or or_7 (or_7_out, and_13_out, and_14_out);
  not not_8 (not_8_out, RSF);
  Demultiplexer #(.select(4)) demultiplexer_3 (
    .out8(demultiplexer_3_out8), .out9(demultiplexer_3_out9), .out10(demultiplexer_3_out10),
    .out12(demultiplexer_3_out12), .out13(demultiplexer_3_out13), .out14(demultiplexer_3_out14), .in(1'b1),
    .sel(BitmaskReg));  // open: out0, out1, out2, out3, out4, out5, out6, out7, out11, out15
  and and_15 (and_15_out, HBenable, WDB);
  and and_16 (and_16_out, MBenable, WDB);
  and and_17 (and_17_out, LBenable, WDB);
  Demultiplexer #(.select(3)) demultiplexer_4 (
    .out0(demultiplexer_4_out0), .out1(demultiplexer_4_out1), .out2(demultiplexer_4_out2),
    .out3(demultiplexer_4_out3), .out4(demultiplexer_4_out4), .out5(demultiplexer_4_out5),
    .out6(demultiplexer_4_out6), .out7(demultiplexer_4_out7), .in(or_7_out), .sel(controlled_buffer_17_out));
  assign controlled_buffer_17_out = RSF ? MicrocodeLocation[2:0] : 3'bz;  // Controlled_Buffer controlled_buffer_17
  assign controlled_buffer_17_out = not_8_out ? TestFlagsRegister_q : 3'bz;  // Controlled_Buffer controlled_buffer_18
  or or_8 (ShortWideInst, demultiplexer_3_out8, demultiplexer_3_out9, demultiplexer_3_out10, demultiplexer_3_out12, demultiplexer_3_out13, demultiplexer_3_out14);
  not not_9 (BMset, comparator_3_eq);
  Comparator #(.mode("unsigned"), .width(4)) comparator_3 (
    .a(BitmaskReg), .b(4'b1111), .eq(comparator_3_eq));  // open: gt, lt
  not not_10 (not_10_out, WBR);
  and and_18 (and_18_out, not_10_out, ARenable);
  and and_19 (and_19_out, ARenable, RRD);
  not not_11 (not_11_out, WBR);
  and and_20 (and_20_out, not_11_out, BRenable);
  and and_21 (and_21_out, BRenable, RRD);
  not not_12 (not_12_out, EvenParityFlag);
  Pull_Resistor pull_resistor_7 (.node(AddressBuffer[3:0]));
  or or_9 (or_9_out, and_19_out, RESET);
  or or_10 (or_10_out, and_21_out, RESET);
  not not_13 (not_13_out, ZeroFlag);
  not not_14 (not_14_out, CarryFlag);
  not not_15 (not_15_out, BorrowFlag);
  Register #(.trigger("falling"), .width(4)) ARegister (
    .D(AddressBuffer[3:0]), .en(and_18_out), .clk(CLK), .Q(AReg), .clr(or_9_out));
  Register #(.trigger("falling"), .width(4)) BRegister (
    .D(AddressBuffer[3:0]), .en(and_20_out), .clk(CLK), .Q(BReg), .clr(or_10_out));
  and and_22 (and_22_out, demultiplexer_4_out0, ZeroFlag);
  and and_23 (and_23_out, demultiplexer_4_out1, CarryFlag);
  and and_24 (and_24_out, demultiplexer_4_out2, BorrowFlag);
  and and_25 (and_25_out, demultiplexer_4_out3, EvenParityFlag);
  and and_26 (and_26_out, demultiplexer_4_out4, not_13_out);
  and and_27 (and_27_out, demultiplexer_4_out5, not_14_out);
  and and_28 (and_28_out, demultiplexer_4_out6, not_15_out);
  and and_29 (and_29_out, demultiplexer_4_out7, not_12_out);
  or or_11 (or_11_out, demultiplexer_4_out1, demultiplexer_4_out5);
  or or_12 (or_12_out, demultiplexer_4_out2, demultiplexer_4_out6);
  and and_30 (CarryFlagReset, or_11_out, RSF);
  and and_31 (BorrowFlagReset, or_12_out, RSF);
  or or_13 (or_13_out, INC, DEC);
  or or_14 (FlagResult, and_22_out, and_23_out, and_24_out, and_25_out, and_26_out, and_27_out, and_28_out, and_29_out);
  or or_15 (or_15_out, HSPenable, MSPenable, LSPenable);
  and and_32 (and_32_out, RBR, HPCenable);
  and and_33 (and_33_out, or_13_out, CLK);
  or or_16 (or_16_out, and_33_out, and_34_out);
  and and_34 (and_34_out, CLK, and_37_out);
  or or_17 (or_17_out, FlagResult, and_32_out);
  and and_35 (and_35_out, INC, CLK);
  and and_36 (and_36_out, CLK, or_17_out);
  and and_37 (and_37_out, RBR, HSPenable);
  and and_38 (and_38_out, or_15_out, or_16_out);
  or or_18 (or_18_out, and_35_out, and_36_out);
  not not_16 (not_16_out, and_38_out);
  Counter #(.max('hfff), .trigger("falling"), .width(12)) u_ProgramCounter (
    .clr(RESET), .load(or_17_out), .up(1'b1), .count(LPCenable), .clk(or_18_out), .D(AddressBuffer),
    .Q(ProgramCounter));  // open: carry
  Pull_Resistor pull_resistor_8 (.node(pull_resistor_8_node));
  Pull_Resistor #(.pull(1)) pull_resistor_9 (.node(pull_resistor_9_node));
  // Probe on StackPointer
  and and_39 (and_39_out, LPCenable, UAR);
  and and_40 (and_40_out, LSPenable, UAR);
  WideCounterWithSR widecounterwithsr_1 (
    .LOAD(and_37_out), .RESET(pull_resistor_8_node), .SET(RESET), .UPDOWN(DEC), .DATA(AddressBuffer),
    .CLK(not_16_out), .NXTIN(pull_resistor_9_node), .DATAOUT(StackPointer));  // open: NXTOUT
  assign controlled_buffer_19_out = and_39_out ? ProgramCounter : 12'bz;  // Controlled_Buffer controlled_buffer_19
  assign controlled_buffer_19_out = and_40_out ? StackPointer : 12'bz;  // Controlled_Buffer controlled_buffer_20
  and and_41 (and_41_out, AAD, clock_2_out);
  Clock clock_2 (.out(clock_2_out));
  and and_42 (and_42_out, UAR, CLK);
  and and_43 (and_43_out, CLK, TFenable, INC);
  and and_44 (and_44_out, TFenable, RBR);
  and and_45 (and_45_out, TFenable, RBR);
  xor xor_1 (xor_1_out, AReg[3], pull_resistor_10_node);
  Pull_Resistor pull_resistor_10 (.node(pull_resistor_10_node));
  Adder #(.width(4)) adder_1 (.a(AReg), .b(BReg), .out(ALUresult), .cin(CarryFlag), .cout(adder_1_cout));
  D_Flip_Flop #(.trigger("falling")) u_CarryFlag (
    .D(adder_1_cout), .clk(and_41_out), .Q(CarryFlag), .reset(or_19_out));  // open: Qn, preset
  or or_19 (or_19_out, RESET, CarryFlagReset);
  or or_20 (or_20_out, and_42_out, and_43_out, and_44_out);
  nor nor_1 (nor_1_out, LPCenable, LSPenable);
  and and_46 (and_46_out, nor_1_out, UAR);
  nor nor_2 (ZeroFlag, AReg[0], AReg[1], AReg[2], AReg[3]);
  xor xor_2 (xor_2_out, AReg[2], xor_1_out);
  D_Flip_Flop u_BorrowFlag (.Q(BorrowFlag));  // open: D, clk, Qn, preset, reset
  or or_21 (or_21_out, and_44_out, and_42_out);
  assign controlled_buffer_19_out = and_46_out ? AddressBuffer : 12'bz;  // Controlled_Buffer controlled_buffer_21
  assign controlled_buffer_19_out = and_45_out ? AddressBuffer : 12'bz;  // Controlled_Buffer controlled_buffer_22
  xor xor_3 (xor_3_out, AReg[1], xor_2_out);
  Pull_Resistor pull_resistor_11 (.node(pull_resistor_11_node));
  Pull_Resistor pull_resistor_12 (.node(pull_resistor_12_node));
  Pull_Resistor #(.pull(1)) pull_resistor_13 (.node(pull_resistor_13_node));
  xor xor_4 (EvenParityFlag, AReg[0], xor_3_out);
  // Probe on ADDRESS
  WideCounterWithSR widecounterwithsr_2 (
    .LOAD(or_21_out), .RESET(RESET), .SET(pull_resistor_11_node), .UPDOWN(pull_resistor_12_node),
    .DATA(controlled_buffer_19_out), .CLK(or_20_out), .NXTIN(pull_resistor_13_node), .DATAOUT(ADDRESS));  // open: NXTOUT

  // Other names for the same wires on the sheet: Write = WDB

  // Notes on the sheet:
  //   Check if Bitmask is needed
  //   contents of Microcode (hex, n*v repeats v):
  //   0 8e 85 70 8e 85 10 f2 8e 85 7 22*0 8e 85 70 8e 85 10 8e 85 20 8e 85 30 62 f3 11 8e 85 7 14*0 8e 85
  //   70 6e 10 6e 20 6e 30 62 10 f2 8e 85 7 17*0 8e 85 70 6e 10 6e 20 6e 30 62 f3 11 8e 85 7 5*0 7 107*0
  //   8e 85 60 8e 85 10 8e 85 20 8e 85 30 86 8e 85 7 112*0 1b 42 8e 85 7 91*0 43 4e 52 8e 85 7 26*0 8e 85
  //   70 f4 8e 85 7 28*0 8e 85 10 7e 8e 85 20 7e 8e 85 30 f2 85 7
  //   contents of rom_1 (hex, n*v repeats v):
  //   0 4 1 1 4 0 0 8 0 4 0 1 4 1 0 8 1 4 2 0 8 1 4 3 0 8 f 1 2 4 0 0 8 2 5 2 0 8 b 1 4 0 0 8 e 1 4 1 0 8
  //   2 4 1 0 8 2 5 3 0 8 b 1 4 1 0 8 e 1 4 3 0 8 7 5 9 1 0 0 8 d 4
  //   Action
  //   Location
  //   Hack to make SWP work!
  //   for some reason gets clocked from 01d to 03e?
  //   0000 0001 1101 +1
  //   = 0000 0011 1110 ???
  //   0000 0001 1101 -1
  //   = 1110 0001 1100 ???
endmodule
